# Fritzing sketch fritzing_schematic (saved by Fritzing 1.0.4)
perfboards: 1

parts:
  S1 = Pushbutton [package="[THT]"]
  S2 = Pushbutton [package="[THT]"]
  S3 = Pushbutton [package="[THT]"]
  LED1 = LED - 5mm [color="Blue (470nm)" current=0.030A package="5 mm [THT]"]
  LED2 = LED - 5mm [color="Blue (470nm)" current=0.030A package="5 mm [THT]"]
  LED3 = LED - 5mm [color="Blue (470nm)" current=0.030A package="5 mm [THT]"]
  R1 = Resistor [tolerance=±5% power=0.25W resistance=100 package=THT]
  R2 = Resistor [tolerance=±5% power=0.25W resistance=100 package=THT]
  R3 = Resistor [tolerance=±5% power=0.25W resistance=100 package=THT]
  S4 = Pushbutton [package="[THT]"]
  S5 = Pushbutton [package="[THT]"]
  LED4 = LED - 5mm [color="Green (560nm)" current=0.030A package="5 mm [THT]"]
  LED5 = LED - 5mm [color="Green (560nm)" current=0.030A package="5 mm [THT]"]
  LED6 = LED - 5mm [color="Green (560nm)" current=0.030A package="5 mm [THT]"]
  R4 = Resistor [tolerance=±5% power=0.25W resistance=220 package=THT]
  R5 = Resistor [tolerance=±5% power=0.25W resistance=220 package=THT]
  R6 = Resistor [tolerance=±5% power=0.25W resistance=220 package=THT]
  J1 = screw terminal, 4 pins [part_number="Encoder Terminal"]
  Mod1 = Raspberry Pi Pico
  J2 = screw terminal, 3 pins [part_number="To Mainboard Terminal"]
  U1 = Sharp PC817 [part_number=LTV817 package=THT]
  R7 = Resistor [tolerance=±5% power=0.25W resistance=1k package=THT]
  R8 = Resistor [tolerance=±5% power=0.25W resistance=1k package=THT]
  U2 = Sharp PC817 [part_number=LTV817 package=THT]
  S6 = Pushbutton [package="[THT]"]
  D1 = Schottky Diode [part_number=1N5819 package="300 mil [THT]"]  # not connected

nets:
  GND: S1.Pin_1, S1.Pin_2, S2.Pin_1, S2.Pin_2, S3.Pin_1, S3.Pin_2, R1.Pin_1, R2.Pin_1, R3.Pin_1, S4.Pin_1, S4.Pin_2, S5.Pin_1, S5.Pin_2, R4.Pin_1, R5.Pin_1, R6.Pin_0, J1.pin2, Mod1.pin_3, Mod1.pin_23, Mod1.pin_28, Mod1.pin_33, Mod1.pin_38, J2.pin3, U1.Pin_3, R7.Pin_0, R8.Pin_0, U2.Pin_3, S6.Pin_1, S6.Pin_2
  1X: S1.Pin_3, S1.Pin_4, Mod1.pin_20
  10X: S2.Pin_3, S2.Pin_4, Mod1.pin_22
  100X: S3.Pin_3, S3.Pin_4, Mod1.pin_25
  N1: LED1.cathode, R2.Pin_0
  1X_LED: LED1.anode, Mod1.pin_19
  N2: LED2.cathode, R3.Pin_0
  10X_LED: LED2.anode, Mod1.pin_21
  N3: LED3.cathode, R1.Pin_0
  100X_LED: LED3.anode, Mod1.pin_24
  X: S4.Pin_3, S4.Pin_4, Mod1.pin_7
  Y: S5.Pin_3, S5.Pin_4, Mod1.pin_17
  N4: LED4.cathode, R6.Pin_1
  X_Axis_LED: LED4.anode, Mod1.pin_6
  N5: LED5.cathode, R4.Pin_0
  Y_Axis_LED: LED5.anode, Mod1.pin_16
  N6: LED6.cathode, R5.Pin_0
  Z_Axis_LED: LED6.anode, Mod1.pin_26
  V_SYS: J1.pin1, Mod1.pin_39
  A: J1.pin3, U1.Pin_1
  B: J1.pin4, U2.Pin_1
  UART_TX: Mod1.pin_1, J2.pin1
  A_3V3: Mod1.pin_14, U1.Pin_4
  B_3V3: Mod1.pin_15, U2.Pin_4
  Z: Mod1.pin_27, S6.Pin_3, S6.Pin_4
  5V: J2.pin2
  N7: U1.Pin_2, R7.Pin_1
  N8: R8.Pin_1, U2.Pin_2

notes:
  ENCODER
  TO_MAINBOARD
  PICO mounted underneath

custom parts:
  Raspberry Pi Pico: Raspberry Pi Pico. Based around the RP2040 microcontroller the Pico is a low cost microcontroller device bringing Raspberry Pi quality, cost, and easy of use to the microcontroller space. Jan 2021, Split part in to two versions: SMD (this one) and tht. This one is single sided and uses the castellation pads to solder the module to the board (no holes, other than for the USB connector!). The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
